// Logisim project s-mips.circ as structural Verilog: 18 circuits, main circuit S-MIPS Board
module S_MIPS_Board (
  input  DESHABILITAR_DISPATCHER,
  output halt
);

  wire button_1_out, CLK, CS, d_ff_1_q, LCLR, LoadRAM, LoadRAMOn, LW, R_R_W, R_W, ram_dispatcher_1_finished,
       RCS, Reset_out, RST, TTY_EN;
  wire [2:0] KDB;
  wire [3:0] LMask, Mask, ram_1_read_time, ram_1_write_time, RMask;
  wire [6:0] KDB_DATA, TTY_DATA;
  wire [15:0] Addr, LAddr, RAddr;
  wire [31:0] I0, I1, I2, I3, LData, ram_1_data_out_0, ram_1_data_out_1, ram_1_data_out_2, ram_1_data_out_3,
       RI0, RI1, RI2, RI3;

  TTY #(.rows(25), .cols(80)) tty_1 (.data(TTY_DATA), .clk(CLK), .we(TTY_EN), .clr(RST));
  not not_1 (LoadRAMOn, ram_dispatcher_1_finished);
  RAM_Dispatcher ram_dispatcher_1 (
    .WriteTime(ram_1_write_time), .Clock(CLK), .Data(LData), .Address(LAddr), .Mask(LMask),
    .Finished(ram_dispatcher_1_finished), .Write(LW), .CLR(LCLR));
  Keyboard #(.buflen(64)) keyboard_1 (.clk(CLK), .re(KDB[0]), .avail(KDB[2]), .data(KDB_DATA));  // open: clr
  RAM ram_1 (
    .Address(RAddr), .Data_Out_0(ram_1_data_out_0), .Data_Out_1(ram_1_data_out_1),
    .Data_Out_2(ram_1_data_out_2), .Data_Out_3(ram_1_data_out_3), .Data_In_0(RI0), .Data_In_1(RI1),
    .Data_In_2(RI2), .Data_In_3(RI3), .Mask(RMask), .nRead_Write(R_R_W), .Chip_Select(RCS),
    .Read_Time(ram_1_read_time), .Reset(button_1_out), .Write_Time(ram_1_write_time));
  Button button_1 (.out(button_1_out));
  D_Flip_Flop d_ff_1 (.clk(CLK), .D(1'b1), .Q(d_ff_1_q), .reset(Reset_out));  // open: Qn, preset, en
  Button Reset (.out(Reset_out));
  S_MIPS s_mips_1 (
    .Kbd_Enable(KDB[0]), .Address(Addr), .Kbd_Clear(KDB[1]), .Kbd_Available(KDB[2]), .RAM_In_0(I0),
    .Kbd_ASCII_Data(KDB_DATA), .RAM_In_1(I1), .TTY_Enable(TTY_EN), .RAM_In_2(I2), .RAM_In_3(I3),
    .TTY_ASCII_Data(TTY_DATA), .Reset(RST), .RAM_Out_0(ram_1_data_out_0), .Clock(CLK),
    .RAM_Out_1(ram_1_data_out_1), .Stop(halt), .RAM_Out_2(ram_1_data_out_2), .RAM_Out_3(ram_1_data_out_3),
    .Mask(Mask), .Read_Time(ram_1_read_time), .Write_Time(ram_1_write_time), .nRead_Write(R_W),
    .Chip_Select(CS));
  D_Flip_Flop d_ff_2 (.clk(CLK), .D(d_ff_1_q), .Qn(LCLR), .reset(Reset_out));  // open: Q, preset, en
  or or_1 (RST, LCLR, LoadRAM);
  Clock clock_1 (.out(CLK));
  Multiplexer #(.width(32), .enable("false")) multiplexer_1 (.in0(I0), .in1(LData), .out(RI0), .sel(LoadRAM));
  Multiplexer #(.width(32), .enable("false")) multiplexer_2 (.in0(I1), .in1(LData), .out(RI1), .sel(LoadRAM));
  Multiplexer #(.width(32), .enable("false")) multiplexer_3 (.in0(I2), .in1(LData), .out(RI2), .sel(LoadRAM));
  Multiplexer #(.width(32), .enable("false")) multiplexer_4 (.in0(I3), .in1(LData), .out(RI3), .sel(LoadRAM));
  and and_1 (LoadRAM, ~DESHABILITAR_DISPATCHER, LoadRAMOn);  // AND_Gate
  Multiplexer #(.width(16), .enable("false")) multiplexer_5 (.in0(Addr), .in1(LAddr), .out(RAddr), .sel(LoadRAM));
  Multiplexer #(.width(4), .enable("false")) multiplexer_6 (.in0(Mask), .in1(LMask), .out(RMask), .sel(LoadRAM));
  Multiplexer #(.enable("false")) multiplexer_7 (.in0(CS), .in1(LW), .out(RCS), .sel(LoadRAM));
  Multiplexer #(.enable("false")) multiplexer_8 (.in0(R_W), .in1(LW), .out(R_R_W), .sel(LoadRAM));

  // Notes on the sheet:
  //   NO MODIFICAR
  //   Keyboard
endmodule

module RAM (
  input  [15:0] Address,
  input  [31:0] Data_In_0,
  input  [31:0] Data_In_1,
  input  [31:0] Data_In_2,
  input  [31:0] Data_In_3,
  input  [3:0] Mask,
  input  nRead_Write,
  input  Chip_Select,
  input  Reset,
  output [31:0] Data_Out_0,
  output [31:0] Data_Out_1,
  output [31:0] Data_Out_2,
  output [31:0] Data_Out_3,
  output [3:0] Read_Time,
  output [3:0] Write_Time
);

  wire and_2_out, and_3_out, and_4_out, and_5_out, and_6_out, and_7_out, and_8_out, and_9_out, Changed, CLK,
       comparator_2_eq, comparator_3_eq, comparator_4_eq, comparator_5_eq, comparator_6_eq, Count,
       demultiplexer_3_out0, Idle, Idle_q, Load, Load0, Load1, nand_1_out, or_1_out, or_2_out, or_3_out,
       or_4_out, or_5_out, or_6_out, or_7_out, or_8_out, or_9_out, or_10_out, Proc_q, Update_Mem, Zero_Time;
  wire [3:0] counter_1_q, multiplexer_1_out, subtractor_1_out;
  wire [31:0] register_1_q, register_2_q, register_3_q, register_4_q, register_5_q;

  // Probe on 4'b0011
  // Probe on 4'b0010
  Multiplexer #(.width(4), .enable("false")) multiplexer_1 (
    .in0(4'b0011), .in1(4'b0010), .out(multiplexer_1_out), .sel(nRead_Write));
  or or_1 (or_1_out, Idle, Update_Mem);
  or or_2 (or_2_out, ~Chip_Select, Reset);  // OR_Gate
  Subtractor #(.width(4)) subtractor_1 (.a(multiplexer_1_out), .b(4'b0010), .out(subtractor_1_out));  // open: bin, bout
  Demultiplexer #(.enable("false")) demultiplexer_1 (.out0(Idle), .out1(Load0), .in(Idle_q), .sel(Changed));
  D_Flip_Flop u_Idle (.clk(CLK), .D(or_1_out), .Q(Idle_q), .preset(or_2_out));  // open: Qn, en, reset
  // Probe on counter_1_q
  Counter #(.width(4), .max('hf)) counter_1 (
    .load(Load), .D(subtractor_1_out), .count(Count), .Q(counter_1_q), .clk(CLK), .clr(or_3_out));  // open: carry
  or or_3 (or_3_out, ~Chip_Select, Reset);  // OR_Gate
  Comparator #(.width(4), .mode("unsigned")) comparator_1 (
    .a(4'b0000), .b(counter_1_q), .eq(Zero_Time));  // open: gt, lt
  or or_4 (or_4_out, Count, Load0, Load1);
  Register #(.width(32)) register_1 (.D(Data_In_0), .en(Chip_Select), .Q(register_1_q), .clk(CLK), .clr(or_5_out));
  or or_5 (or_5_out, ~Chip_Select, Reset);  // OR_Gate
  Register #(.width(32)) register_2 (.D(Data_In_1), .en(Chip_Select), .Q(register_2_q), .clk(CLK), .clr(or_6_out));
  or or_6 (or_6_out, ~Chip_Select, Reset);  // OR_Gate
  Register #(.width(32)) register_3 (.D(Data_In_2), .en(Chip_Select), .Q(register_3_q), .clk(CLK), .clr(or_7_out));
  or or_7 (or_7_out, ~Chip_Select, Reset);  // OR_Gate
  Register #(.width(32)) register_4 (.D(Data_In_3), .en(Chip_Select), .Q(register_4_q), .clk(CLK), .clr(or_8_out));
  or or_8 (or_8_out, ~Chip_Select, Reset);  // OR_Gate
  Register #(.width(32)) register_5 (
    .D({{11{1'b1}}, nRead_Write, Mask, Address}), .en(Chip_Select), .Q(register_5_q), .clk(CLK),
    .clr(or_9_out));
  or or_9 (or_9_out, ~Chip_Select, Reset);  // OR_Gate
  D_Flip_Flop Proc (.clk(CLK), .D(or_4_out), .Q(Proc_q), .reset(or_10_out));  // open: Qn, preset, en
  or or_10 (or_10_out, ~Chip_Select, Reset);  // OR_Gate
  Demultiplexer #(.enable("false")) demultiplexer_2 (
    .out0(Count), .out1(Update_Mem), .in(demultiplexer_3_out0), .sel(Zero_Time));
  Demultiplexer #(.enable("false")) demultiplexer_3 (
    .out0(demultiplexer_3_out0), .out1(Load1), .in(Proc_q), .sel(Changed));
  Clock clock_1 (.out(CLK));
  Comparator #(.width(32)) comparator_2 (.a(register_1_q), .b(Data_In_0), .eq(comparator_2_eq));  // open: gt, lt
  Comparator #(.width(32)) comparator_3 (.a(register_2_q), .b(Data_In_1), .eq(comparator_3_eq));  // open: gt, lt
  Comparator #(.width(32)) comparator_4 (.a(register_3_q), .b(Data_In_2), .eq(comparator_4_eq));  // open: gt, lt
  Comparator #(.width(32)) comparator_5 (.a(register_4_q), .b(Data_In_3), .eq(comparator_5_eq));  // open: gt, lt
  Comparator #(.width(32)) comparator_6 (
    .a(register_5_q), .b({{11{1'b1}}, nRead_Write, Mask, Address}), .eq(comparator_6_eq));  // open: gt, lt
  nand nand_1 (nand_1_out, comparator_6_eq, comparator_2_eq, comparator_3_eq, comparator_4_eq, comparator_5_eq);
  and and_1 (Changed, nand_1_out, Chip_Select);
  or or_11 (Load, Count, Load1, Load0);
  and and_2 (and_2_out, Mask[0], Update_Mem, nRead_Write);
  and and_3 (and_3_out, Mask[1], Update_Mem, nRead_Write);
  and and_4 (and_4_out, Mask[2], Update_Mem, nRead_Write);
  and and_5 (and_5_out, Mask[3], Update_Mem, nRead_Write);
  RAM_part #(.addrWidth(16), .dataWidth(32), .bus("separate")) ram_1 (
    .addr(Address), .din(Data_In_0), .data(Data_Out_0), .str(and_2_out), .sel(Chip_Select), .clk(CLK),
    .ld(and_6_out), .clr(Reset));
  and and_6 (and_6_out, ~nRead_Write, Idle);  // AND_Gate
  RAM_part #(.addrWidth(16), .dataWidth(32), .bus("separate")) ram_2 (
    .addr(Address), .din(Data_In_1), .data(Data_Out_1), .str(and_3_out), .sel(Chip_Select), .clk(CLK),
    .ld(and_7_out), .clr(Reset));
  and and_7 (and_7_out, ~nRead_Write, Idle);  // AND_Gate
  RAM_part #(.addrWidth(16), .dataWidth(32), .bus("separate")) ram_3 (
    .addr(Address), .din(Data_In_2), .data(Data_Out_2), .str(and_4_out), .sel(Chip_Select), .clk(CLK),
    .ld(and_8_out), .clr(Reset));
  and and_8 (and_8_out, ~nRead_Write, Idle);  // AND_Gate
  RAM_part #(.addrWidth(16), .dataWidth(32), .bus("separate")) ram_4 (
    .addr(Address), .din(Data_In_3), .data(Data_Out_3), .str(and_5_out), .sel(Chip_Select), .clk(CLK),
    .ld(and_9_out), .clr(Reset));
  and and_9 (and_9_out, ~nRead_Write, Idle);  // AND_Gate

  assign Read_Time = 4'b0011;
  assign Write_Time = 4'b0010;

  // Other names for the same wires on the sheet: M0 = Mask[0]; M1 = Mask[1]; M2 = Mask[2]; M3 = Mask[3];
  //   RW = nRead_Write; CLR = Reset; CS = Chip_Select; Load2 = Count

  // Notes on the sheet:
  //   NO MODIFICAR
  //   excepto quizás los valores RT y WT
  //   BANK0
  //   BANK1
  //   BANK2
  //   BANK3
endmodule

module S_MIPS (
  input  Kbd_Available,
  input  [6:0] Kbd_ASCII_Data,
  input  [31:0] RAM_Out_0,
  input  [31:0] RAM_Out_1,
  input  Reset,
  input  [31:0] RAM_Out_2,
  input  Clock,
  input  [31:0] RAM_Out_3,
  input  [3:0] Read_Time,
  input  [3:0] Write_Time,
  output Kbd_Enable,
  output [15:0] Address,
  output Kbd_Clear,
  output TTY_Enable,
  output [6:0] TTY_ASCII_Data,
  output Stop,
  output [31:0] RAM_In_0,
  output [31:0] RAM_In_1,
  output [31:0] RAM_In_2,
  output [31:0] RAM_In_3,
  output [3:0] Mask,
  output nRead_Write,
  output Chip_Select
);

  wire and_2_out, and_3_out, bitfinder_1_found, br, comparator_1_eq, comparator_2_eq, convert_opcode_1_kbd,
       Fill, Halt, HL_Flag, I, J, jr, mfhi, mflo, not_1_out, not_2_out, pop_push, R, r_ram, Ready, stack, w,
       w_ram;
  wire [1:0] convert_opcode_1_hi_lo_op, State;
  wire [2:0] br_OP;
  wire [3:0] convert_opcode_1_alu_op;
  wire [4:0] R_Reg, RD, RS, RT;
  wire [5:0] Func_Code, OPCODE;
  wire [15:0] and_1_out, BC_Addr, branch_control_1_ram_addr, Const, IO_Addr;
  wire [25:0] J_Dest;
  wire [31:0] ALU_Result, Hi, Inm, Lo, multiplexer_4_out, multiplexer_6_out, multiplexer_8_out, Next_Ctr, PC,
       R_Val, ram_out_select_1_out_8, RegB, SP;
  wire [31:7] RegA;
  wire [31:31] multiplexer_3_out;

  Multiplexer #(.width(16), .enable("false")) multiplexer_1 (
    .in0(BC_Addr), .in1(IO_Addr), .out(Address), .sel(not_1_out));
  not not_1 (not_1_out, comparator_1_eq);
  Comparator #(.width(2)) comparator_1 (.a(State), .b(2'b00), .eq(comparator_1_eq));  // open: gt, lt
  Multiplexer #(.enable("false")) multiplexer_2 (.in0(convert_opcode_1_kbd), .in1(1'b0), .out(Kbd_Enable), .sel(Reset));
  assign and_1_out = 16'h8000 & Const;  // AND_Gate and_1, 16 bits wide
  BitFinder #(.width(16)) bitfinder_1 (.in(and_1_out), .found(bitfinder_1_found));  // open: index
  Multiplexer #(.enable("false")) multiplexer_3 (
    .in0(1'b0), .in1(bitfinder_1_found), .out(multiplexer_3_out[31]), .sel(Fill));
  Multiplexer #(.width(32), .enable("false")) multiplexer_4 (
    .in0({32{1'b1}}), .in1({{25{1'b0}}, Kbd_ASCII_Data}), .out(multiplexer_4_out), .sel(Kbd_Available));
  Convert_Opcode convert_opcode_1 (
    .in_1(OPCODE), .in_2(Func_Code), .ALU_OP(convert_opcode_1_alu_op), .tty(TTY_Enable), .halt(Halt),
    .Fill(Fill), .Hi_Lo_OP(convert_opcode_1_hi_lo_op), .Hi_Lo_FLag(HL_Flag), .mflo(mflo), .mfhi(mfhi),
    .jr(jr), .Branch_OP(br_OP), .Branch(br), .r_ram(r_ram), .w_ram(w_ram), .stack(stack),
    .pop_push(pop_push), .kbd(convert_opcode_1_kbd));
  nor nor_1 (w, br, r_ram, w_ram);
  Multiplexer #(.width(32), .enable("false")) multiplexer_5 (
    .in0({{16{multiplexer_3_out[31]}}, Const}), .in1(multiplexer_4_out), .out(Inm), .sel(Kbd_Enable));
  Register #(.width(32)) register_1 (.D(Next_Ctr), .Q(PC), .clk(Clock), .clr(Reset));  // open: en
  RAM_Out_Select ram_out_select_1 (
    .RAM_Out_0(RAM_Out_0), .RAM_Out_1(RAM_Out_1), .RAM_Out_2(RAM_Out_2), .RAM_Out_3(RAM_Out_3),
    .out_8(ram_out_select_1_out_8), .Program_Counter(PC), .in_1(State), .in_2(Ready));
  // Probe on PC
  Multiplexer #(.width(32), .enable("false")) multiplexer_6 (
    .in0(Inm), .in1(RegB), .out(multiplexer_6_out), .sel(and_2_out));
  and and_2 (and_2_out, R, ~Kbd_Enable);  // AND_Gate
  Instruction_Decoder instruction_decoder_1 (
    .Instruction(ram_out_select_1_out_8), .out_2(OPCODE), .Read1(RS), .Read2(RT), .Destiny(RD),
    .out_6(Func_Code), .out_7(Const), .R(R), .I(I), .J(J), .Destiny_2(J_Dest));
  // Probe on Hi
  not not_2 (not_2_out, Stop);
  Comparator #(.width(2)) comparator_2 (.a(State), .b(2'b00), .eq(comparator_2_eq));  // open: gt, lt
  ALU alu_1 (
    .in_1(convert_opcode_1_alu_op), .in_2({RegA, TTY_ASCII_Data}), .in_3(multiplexer_6_out),
    .out_6(ALU_Result), .Lo(Lo), .in_4(HL_Flag), .in_5(convert_opcode_1_hi_lo_op), .Hi(Hi));
  // Probe on Lo
  and and_3 (and_3_out, not_2_out, comparator_2_eq);
  // Probe on ALU_Result
  Branch_Control branch_control_1 (
    .Program_Counter(PC), .Next(and_3_out), .RAM_Addr(branch_control_1_ram_addr), .Next_Ptr(Next_Ctr),
    .J_Dest(J_Dest), .J(J), .jr(jr), .RS_V({RegA, TTY_ASCII_Data}), .Branch(br), .Br_OP(br_OP), .RT_V(RegB),
    .Branch_Destiny(Const), .Ready(Ready));
  Multiplexer #(.width(16), .enable("false")) multiplexer_7 (
    .in0(branch_control_1_ram_addr), .in1({16{1'b0}}), .out(BC_Addr), .sel(Reset));
  Multiplexer #(.width(32), .enable("false")) multiplexer_8 (
    .in0(RegB), .in1({RegA, TTY_ASCII_Data}), .out(multiplexer_8_out), .sel(stack));
  Register_File register_file_1 (
    .in_1(Clock), .in_2(w), .in_3(RD), .Write_Value(ALU_Result), .in_5(RS), .in_7(RT), .in_8(Reset),
    .out_19({RegA, TTY_ASCII_Data}), .in_10(HL_Flag), .in_12(Lo), .in_15(Hi), .in_16(mflo), .in_17(mfhi),
    .out_21(RegB), .in_6(R_Reg), .RAM_Val(R_Val), .in_11(State), .stack(stack), .pop_push(pop_push), .SP(SP),
    .in_18(Ready));
  State_Machine state_machine_1 (
    .in_1(Clock), .in_2(Reset), .State(State), .in_3(r_ram), .in_4(w_ram), .RW(nRead_Write), .in_5(pop_push),
    .in_6(stack), .in_7(Read_Time), .in_8(Write_Time), .Ready(Ready), .in_9(Halt), .Stop(Stop),
    .in_10(Address));
  RAM_IO ram_io_1 (
    .Dir(ALU_Result), .Value(multiplexer_8_out), .Mask(Mask), .RAM_Addr(IO_Addr), .RAM_In_0(RAM_In_0),
    .RAM_In_1(RAM_In_1), .RAM_In_2(RAM_In_2), .RAM_In_3(RAM_In_3), .in_10(Clock), .in_11(Reset),
    .in_3(State), .Dest_Reg(R_Reg), .RAM_Out_0(RAM_Out_0), .RAM_Out_1(RAM_Out_1), .RAM_Out_2(RAM_Out_2),
    .RAM_Out_3(RAM_Out_3), .RAM_Reading(R_Val), .SP(SP), .in_1(pop_push), .in_2(stack), .Pop_Reg(RD),
    .lw_reg(RT));

  assign Chip_Select = 1'b1;

  // Other names for the same wires on the sheet: KBD_DATA[6:0] = Kbd_ASCII_Data; CLK = Clock; CLR = Reset;
  //   KBD_AVAIL = Kbd_Available; KBD_CLR = Kbd_Clear; RAM_A[15:0] = Address; RAM_INPUT_0[31:0] = RAM_In_0;
  //   RAM_INPUT_1[31:0] = RAM_In_1; RAM_INPUT_2[31:0] = RAM_In_2; RAM_INPUT_3[31:0] = RAM_In_3; RAM_MASK[3:0] = Mask;
  //   RAM_OUTPUT_0[31:0] = RAM_Out_0; RAM_OUTPUT_1[31:0] = RAM_Out_1; RAM_OUTPUT_2[31:0] = RAM_Out_2;
  //   RAM_OUTPUT_3[31:0] = RAM_Out_3; RegA[6:0] = TTY_ASCII_Data; TTY_DATA[6:0] = TTY_ASCII_Data; RW = nRead_Write

  // Notes on the sheet:
  //   RAM ADDRESS
  //   DATA FROM RAM
  //   DATA TO RAM
  //   DATA WRITE MASK
  //   RAM TIMING
  //   RAM CONTROL
  //   KEYBOARD
  //   TTY
  //   SEQUENCING
  //   Constant Manager
  //   Program Counter
endmodule

module RAM_Dispatcher (
  input  [3:0] WriteTime,
  input  Clock,
  input  CLR,
  output [31:0] Data,
  output [15:0] Address,
  output [3:0] Mask,
  output Finished,
  output Write
);

  wire demultiplexer_2_out1, demultiplexer_3_out1, End, IDLE_q, IncAddr, Load, or_1_out, or_2_out, While_q,
       WriteEnd;
  wire [3:0] counter_1_q;
  wire [31:0] CurrentAddress_q;

  Counter #(.width(32), .max('hffffffff)) CurrentAddress (
    .count(IncAddr), .Q({CurrentAddress_q[31:18], Address, CurrentAddress_q[1:0]}), .clk(Clock), .clr(CLR));  // open: load, D, carry
  or or_1 (or_1_out, IncAddr, demultiplexer_3_out1, Finished);
  D_Flip_Flop IDLE (.clk(Clock), .D(or_1_out), .Q(IDLE_q), .preset(CLR));  // open: Qn, en, reset
  Demultiplexer #(.enable("false")) demultiplexer_1 (.out0(Load), .out1(Finished), .in(IDLE_q), .sel(End));
  D_Flip_Flop While (.clk(Clock), .D(or_2_out), .Q(While_q), .reset(CLR));  // open: Qn, preset, en
  or or_2 (or_2_out, Write, Load);
  RAM_part #(.addrWidth(18), .dataWidth(32)) ram_1 (
    .addr({Address, CurrentAddress_q[1:0]}), .data(Data), .clk(Clock));  // open: sel, ld, clr
  Demultiplexer #(.enable("false")) demultiplexer_2 (
    .out0(Write), .out1(demultiplexer_2_out1), .in(While_q), .sel(WriteEnd));
  Decoder #(.select(2)) decoder_1 (
    .out0(Mask[0]), .out1(Mask[1]), .out2(Mask[2]), .out3(Mask[3]), .sel(CurrentAddress_q[1:0]));  // open: en
  Demultiplexer #(.enable("false")) demultiplexer_3 (
    .out0(IncAddr), .out1(demultiplexer_3_out1), .in(demultiplexer_2_out1), .sel(End));
  Counter #(.width(4), .max('hf)) counter_1 (
    .load(Load), .D(WriteTime), .count(Write), .Q(counter_1_q), .clk(Clock));  // open: carry, clr
  Comparator #(.width(32)) comparator_1 (.a(Data), .b({32{1'b1}}), .eq(End));  // open: gt, lt
  Comparator #(.width(4)) comparator_2 (.a(4'b0000), .b(counter_1_q), .eq(WriteEnd));  // open: gt, lt

  // Other names for the same wires on the sheet: CLK = Clock; Count = Write; WT[3:0] = WriteTime
endmodule

module RAM_Out_Select (
  input  [1:0] in_1,
  input  in_2,
  input  [31:0] RAM_Out_0,
  input  [31:0] Program_Counter,
  input  [31:0] RAM_Out_1,
  input  [31:0] RAM_Out_2,
  input  [31:0] RAM_Out_3,
  output [31:0] out_8
);

  wire and_1_out, comparator_1_eq;

  Comparator #(.width(2)) comparator_1 (.a(in_1), .b(2'b00), .eq(comparator_1_eq));  // open: gt, lt
  Multiplexer #(.select(2), .width(32), .disabled(0)) multiplexer_1 (
    .in0(RAM_Out_0), .in1(RAM_Out_1), .in2(RAM_Out_2), .in3(RAM_Out_3), .out(out_8),
    .sel(Program_Counter[3:2]), .en(and_1_out));
  and and_1 (and_1_out, comparator_1_eq, in_2);

  // Other names for the same wires on the sheet: Ready = in_2; State[1:0] = in_1
endmodule

module Instruction_Decoder (
  input  [31:0] Instruction,
  output [5:0] out_2,
  output [4:0] Read1,
  output [4:0] Read2,
  output [4:0] Destiny,
  output [5:0] out_6,
  output [15:0] out_7,
  output [25:0] Destiny_2,
  output R,
  output I,
  output J
);

  wire comparator_1_eq, comparator_2_eq, comparator_3_eq;

  Comparator #(.width(6)) comparator_1 (.a(Instruction[7:2]), .b({6{1'b0}}), .eq(comparator_1_eq));  // open: gt, lt
  Comparator #(.width(6)) comparator_2 (.a(Instruction[7:2]), .b({6{1'b1}}), .eq(comparator_2_eq));  // open: gt, lt
  Comparator #(.width(6)) comparator_3 (.a(Instruction[7:2]), .b(6'b111000), .eq(comparator_3_eq));  // open: gt, lt
  Comparator #(.width(6)) comparator_4 (.a(Instruction[7:2]), .b(6'b000010), .eq(J));  // open: gt, lt
  or or_1 (R, comparator_1_eq, comparator_2_eq, comparator_3_eq);
  Multiplexer #(.width(5), .enable("false")) multiplexer_1 (
    .in0(Instruction[12:8]), .in1(Instruction[23:19]), .out(Destiny), .sel(R));
  // Probe on {Instruction[23:16], Instruction[31:24]}
  nor nor_1 (I, R, J);

  assign Destiny_2 = {Instruction[1:0], Instruction[15:8], Instruction[23:16], Instruction[31:24]};
  assign out_2 = Instruction[7:2];
  assign out_6 = Instruction[29:24];
  assign out_7 = {Instruction[23:16], Instruction[31:24]};
  assign Read1 = {Instruction[1:0], Instruction[15:13]};
  assign Read2 = Instruction[12:8];

  // Other names for the same wires on the sheet: Const[15:0] = {Instruction[23:16], Instruction[31:24]};
  //   FUNC_CODE[5:0] = Instruction[29:24]; X[4:0] = {Instruction[18:16], Instruction[31:30]};
  //   RD[4:0] = Instruction[23:19]; RT[4:0] = Instruction[12:8]; RS[4:0] = {Instruction[1:0], Instruction[15:13]};
  //   OPCODE[5:0] = Instruction[7:2]
endmodule

module Register_File (
  input  in_1,
  input  in_2,
  input  [4:0] in_3,
  input  [31:0] Write_Value,
  input  [4:0] in_5,
  input  [4:0] in_6,
  input  [4:0] in_7,
  input  in_8,
  input  [31:0] RAM_Val,
  input  in_10,
  input  [1:0] in_11,
  input  [31:0] in_12,
  input  stack,
  input  pop_push,
  input  [31:0] in_15,
  input  in_16,
  input  in_17,
  input  in_18,
  output [31:0] out_19,
  output [31:0] SP,
  output [31:0] out_21
);

  wire and_1_out, comparator_1_eq, comparator_2_eq, HL_FLag_t, w0A, w0B, w0C, w0D, w0E, w0F, w01, w1A, w1B,
       w1C, w1D, w1E, w1F, w02, w03, w04, w05, w06, w07, w08, w09, w10, w11, w12, w13, w14, w15, w16, w17,
       w18, w19, was_stack;
  wire [4:0] multiplexer_1_out, multiplexer_4_out;
  wire [31:0] adder_1_out, adder_2_out, Hi_Out, Lo_Out, multiplexer_2_out, multiplexer_3_out,
       multiplexer_5_out, multiplexer_7_out, multiplexer_8_out, r00, r0A, r0B, r0C, r0D, r0E, r0F, r01, r1A,
       r1B, r1C, r1D, r1E, r02, r03, r04, r05, r06, r07, r08, r09, r10, r11, r12, r13, r14, r15, r16, r17,
       r18, r19, write;

  Comparator #(.width(2)) comparator_1 (.a(in_11), .b(2'b10), .eq(comparator_1_eq));  // open: gt, lt
  // Probe on in_5
  // Probe on in_7
  Multiplexer #(.width(5), .enable("false")) multiplexer_1 (
    .in0(in_3), .in1(in_6), .out(multiplexer_1_out), .sel(comparator_1_eq));
  Multiplexer #(.width(32), .enable("false")) multiplexer_2 (
    .in0(Write_Value), .in1(RAM_Val), .out(multiplexer_2_out), .sel(comparator_1_eq));
  Multiplexer #(.width(32), .enable("false")) multiplexer_3 (
    .in0(32'h4), .in1(32'hfffffffc), .out(multiplexer_3_out), .sel(pop_push));
  Decoder #(.select(5), .disabled(0)) decoder_1 (
    .out1(w01), .out2(w02), .out3(w03), .out4(w04), .out5(w05), .out6(w06), .out7(w07), .out8(w08),
    .out9(w09), .out10(w0A), .out11(w0B), .out12(w0C), .out13(w0D), .out14(w0E), .out15(w0F), .out16(w10),
    .out17(w11), .out18(w12), .out19(w13), .out20(w14), .out21(w15), .out22(w16), .out23(w17), .out24(w18),
    .out25(w19), .out26(w1A), .out27(w1B), .out28(w1C), .out29(w1D), .out30(w1E), .out31(w1F),
    .sel(multiplexer_4_out), .en(in_2));  // open: out0
  Multiplexer #(.width(5), .enable("false")) multiplexer_4 (
    .in0(multiplexer_1_out), .in1({5{1'b1}}), .out(multiplexer_4_out), .sel(stack));
  Adder #(.width(32)) adder_1 (.a(multiplexer_3_out), .b(SP), .out(adder_1_out));  // open: cin, cout
  Multiplexer #(.width(32), .enable("false")) multiplexer_5 (
    .in0(multiplexer_2_out), .in1(adder_1_out), .out(multiplexer_5_out), .sel(stack));
  Comparator #(.width(5)) comparator_2 (.a(in_6), .b({5{1'b1}}), .eq(comparator_2_eq));  // open: gt, lt
  Multiplexer #(.width(32), .enable("false")) multiplexer_6 (
    .in0(multiplexer_5_out), .in1(adder_2_out), .out(write), .sel(and_1_out));
  Adder #(.width(32)) adder_2 (.a(multiplexer_5_out), .b(32'h4), .out(adder_2_out));  // open: cin, cout
  and and_1 (and_1_out, was_stack, comparator_2_eq);
  Register #(.width(32)) register_1 (.D(in_12), .en(HL_FLag_t), .Q(Lo_Out), .clk(in_1), .clr(in_8));
  Register #(.width(32)) register_2 (.D(in_15), .en(HL_FLag_t), .Q(Hi_Out), .clk(in_1), .clr(in_8));
  D_Flip_Flop d_ff_1 (.clk(in_1), .D(stack), .Q(was_stack), .en(in_18));  // open: Qn, preset, reset
  Register #(.width(32)) register_3 (.Q(r00), .clk(in_1), .clr(in_8));  // open: D, en
  Register #(.width(32)) register_4 (.D(write), .en(w04), .Q(r04), .clk(in_1), .clr(in_8));
  Register #(.width(32)) register_5 (.D(write), .en(w08), .Q(r08), .clk(in_1), .clr(in_8));
  Register #(.width(32)) register_6 (.D(write), .en(w0C), .Q(r0C), .clk(in_1), .clr(in_8));
  Register #(.width(32)) register_7 (.D(write), .en(w10), .Q(r10), .clk(in_1), .clr(in_8));
  Register #(.width(32)) register_8 (.D(write), .en(w14), .Q(r14), .clk(in_1), .clr(in_8));
  Register #(.width(32)) register_9 (.D(write), .en(w18), .Q(r18), .clk(in_1), .clr(in_8));
  Register #(.width(32)) register_10 (.D(write), .en(w1C), .Q(r1C), .clk(in_1), .clr(in_8));
  Register #(.width(32)) register_11 (.D(write), .en(w01), .Q(r01), .clk(in_1), .clr(in_8));
  Register #(.width(32)) register_12 (.D(write), .en(w05), .Q(r05), .clk(in_1), .clr(in_8));
  Register #(.width(32)) register_13 (.D(write), .en(w09), .Q(r09), .clk(in_1), .clr(in_8));
  Register #(.width(32)) register_14 (.D(write), .en(w0D), .Q(r0D), .clk(in_1), .clr(in_8));
  Register #(.width(32)) register_15 (.D(write), .en(w11), .Q(r11), .clk(in_1), .clr(in_8));
  Register #(.width(32)) register_16 (.D(write), .en(w15), .Q(r15), .clk(in_1), .clr(in_8));
  Register #(.width(32)) register_17 (.D(write), .en(w19), .Q(r19), .clk(in_1), .clr(in_8));
  Register #(.width(32)) register_18 (.D(write), .en(w1D), .Q(r1D), .clk(in_1), .clr(in_8));
  Register #(.width(32)) register_19 (.D(write), .en(w02), .Q(r02), .clk(in_1), .clr(in_8));
  Register #(.width(32)) register_20 (.D(write), .en(w06), .Q(r06), .clk(in_1), .clr(in_8));
  Register #(.width(32)) register_21 (.D(write), .en(w0A), .Q(r0A), .clk(in_1), .clr(in_8));
  Register #(.width(32)) register_22 (.D(write), .en(w0E), .Q(r0E), .clk(in_1), .clr(in_8));
  Register #(.width(32)) register_23 (.D(write), .en(w12), .Q(r12), .clk(in_1), .clr(in_8));
  Register #(.width(32)) register_24 (.D(write), .en(w16), .Q(r16), .clk(in_1), .clr(in_8));
  Register #(.width(32)) register_25 (.D(write), .en(w1A), .Q(r1A), .clk(in_1), .clr(in_8));
  Register #(.width(32)) register_26 (.D(write), .en(w1E), .Q(r1E), .clk(in_1), .clr(in_8));
  Register #(.width(32)) register_27 (.D(write), .en(w03), .Q(r03), .clk(in_1), .clr(in_8));
  Register #(.width(32)) register_28 (.D(write), .en(w07), .Q(r07), .clk(in_1), .clr(in_8));
  Register #(.width(32)) register_29 (.D(write), .en(w0B), .Q(r0B), .clk(in_1), .clr(in_8));
  Register #(.width(32)) register_30 (.D(write), .en(w0F), .Q(r0F), .clk(in_1), .clr(in_8));
  Register #(.width(32)) register_31 (.D(write), .en(w13), .Q(r13), .clk(in_1), .clr(in_8));
  Register #(.width(32)) register_32 (.D(write), .en(w17), .Q(r17), .clk(in_1), .clr(in_8));
  Register #(.width(32)) register_33 (.D(write), .en(w1B), .Q(r1B), .clk(in_1), .clr(in_8));
  Register #(.width(32)) u_SP (.D(write), .en(w1F), .Q(SP), .clk(in_1), .clr(in_8));
  // Probe on SP
  Multiplexer #(.select(5), .width(32), .disabled(0), .enable("false")) multiplexer_7 (
    .in0(r00), .in1(r01), .in2(r02), .in3(r03), .in4(r04), .in5(r05), .in6(r06), .in7(r07), .in8(r08),
    .in9(r09), .in10(r0A), .in11(r0B), .in12(r0C), .in13(r0D), .in14(r0E), .in15(r0F), .in16(r10),
    .in17(r11), .in18(r12), .in19(r13), .in20(r14), .in21(r15), .in22(r16), .in23(r17), .in24(r18),
    .in25(r19), .in26(r1A), .in27(r1B), .in28(r1C), .in29(r1D), .in30(r1E), .in31(SP),
    .out(multiplexer_7_out), .sel(in_5));
  Multiplexer #(.select(5), .width(32), .disabled(0), .enable("false")) multiplexer_8 (
    .in0(r00), .in1(r01), .in2(r02), .in3(r03), .in4(r04), .in5(r05), .in6(r06), .in7(r07), .in8(r08),
    .in9(r09), .in10(r0A), .in11(r0B), .in12(r0C), .in13(r0D), .in14(r0E), .in15(r0F), .in16(r10),
    .in17(r11), .in18(r12), .in19(r13), .in20(r14), .in21(r15), .in22(r16), .in23(r17), .in24(r18),
    .in25(r19), .in26(r1A), .in27(r1B), .in28(r1C), .in29(r1D), .in30(r1E), .in31(SP),
    .out(multiplexer_8_out), .sel(in_7));
  // Probe on out_19
  Multiplexer #(.width(32), .enable("false")) multiplexer_9 (
    .in0(multiplexer_7_out), .in1(Lo_Out), .out(out_19), .sel(in_16));
  // Probe on out_21
  Multiplexer #(.width(32), .enable("false")) multiplexer_10 (
    .in0(multiplexer_8_out), .in1(Hi_Out), .out(out_21), .sel(in_17));

  // Other names for the same wires on the sheet: Hi[31:0] = in_15; HL_FLag = in_10; Lo[31:0] = in_12; mfhi = in_17;
  //   mflo = in_16; r1F[31:0] = SP; RAM_Reg[4:0] = in_6; Read1[4:0] = in_5; Read2[4:0] = in_7; Ready = in_18;
  //   rst = in_8; State[1:0] = in_11; T = in_1; w = in_2

  // Notes on the sheet:
  //   Read Indexs
  //   Stack Updater
  //   Write Selection
  //   REGISTERS
  //   Output 1 Selection
  //   Output 2 Selection 
endmodule

module ALU (
  input  [3:0] in_1,
  input  [31:0] in_2,
  input  [31:0] in_3,
  input  in_4,
  input  [1:0] in_5,
  output [31:0] out_6,
  output [31:0] Lo,
  output [31:0] Hi
);

  wire clock_1_out, comparator_1_lt, comparator_2_lt;
  wire [31:0] Add, \and , Div, Divu, Mod, Modu, Mult_Hi, Mult_Lo, Mulu_Hi, Mulu_Lo, \nor , \or , rnd, slt,
       sltu, Sub, \xor ;

  // Probe on in_2
  // Probe on in_3
  Clock clock_1 (.out(clock_1_out));
  Adder #(.width(32)) adder_1 (.a(in_2), .b(in_3), .out(Add));  // open: cin, cout
  Subtractor #(.width(32)) subtractor_1 (.a(in_2), .b(in_3), .out(Sub));  // open: bin, bout
  Signed_Mult signed_mult_1 (.in_1(in_2), .in_2(in_3), .Lo(Mult_Lo), .Hi(Mult_Hi));
  Multiplier #(.width(32)) multiplier_1 (.a(in_2), .b(in_3), .out(Mulu_Lo), .cout(Mulu_Hi));  // open: cin
  Signed_Div signed_div_1 (.in_1(in_2), .in_2(in_3), .Quotient(Div), .Remainder(Mod));
  Divider #(.width(32)) divider_1 (.a(in_2), .b(in_3), .out(Divu), .rem(Modu));  // open: upper
  assign \and  = in_2 & in_3;  // AND_Gate and_1, 32 bits wide
  assign \or  = in_2 | in_3;  // OR_Gate or_1, 32 bits wide
  assign \nor  = ~(in_2 | in_3);  // NOR_Gate nor_1, 32 bits wide
  assign \xor  = in_2 ^ in_3;  // XOR_Gate xor_1, 32 bits wide
  Random #(.width(32)) random_1 (.clk(clock_1_out), .out(rnd));  // open: next, clr
  Multiplexer #(.select(4), .width(32), .enable("false")) multiplexer_1 (
    .in0({32{1'b0}}), .in1(Add), .in2(Sub), .in3(slt), .in4(sltu), .in5(\and ), .in6(\or ), .in7(\nor ),
    .in8(\xor ), .in9(rnd), .out(out_6), .sel(in_1));  // open: in10, in11, in12, in13, in14, in15
  Multiplexer #(.select(2), .width(32)) multiplexer_2 (
    .in0(Mult_Lo), .in1(Mulu_Lo), .in2(Div), .in3(Divu), .out(Lo), .sel(in_5), .en(in_4));
  Multiplexer #(.select(2), .width(32)) multiplexer_3 (
    .in0(Mult_Hi), .in1(Mulu_Hi), .in2(Mod), .in3(Modu), .out(Hi), .sel(in_5), .en(in_4));
  Multiplexer #(.width(32), .enable("false")) multiplexer_4 (
    .in0({32{1'b0}}), .in1(32'h1), .out(slt), .sel(comparator_1_lt));
  Comparator #(.width(32)) comparator_1 (.a(in_2), .b(in_3), .lt(comparator_1_lt));  // open: gt, eq
  Multiplexer #(.width(32), .enable("false")) multiplexer_5 (
    .in0({32{1'b0}}), .in1(32'h1), .out(sltu), .sel(comparator_2_lt));
  Comparator #(.width(32), .mode("unsigned")) comparator_2 (.a(in_2), .b(in_3), .lt(comparator_2_lt));  // open: gt, eq
  // Probe on Lo
  // Probe on Hi

  // Other names for the same wires on the sheet: A[31:0] = in_2; B[31:0] = in_3; Hi_Lo_Flag = in_4;
  //   Hi_Lo_OP[1:0] = in_5; OP[3:0] = in_1; Result[31:0] = out_6
endmodule

module Convert_Opcode (
  input  [5:0] in_1,
  input  [5:0] in_2,
  output tty,
  output halt,
  output mflo,
  output mfhi,
  output jr,
  output r_ram,
  output w_ram,
  output stack,
  output pop_push,
  output kbd,
  output [1:0] Hi_Lo_OP,
  output Hi_Lo_FLag,
  output [3:0] ALU_OP,
  output Fill,
  output [2:0] Branch_OP,
  output Branch
);

  wire add, addi, \and , andi, beq, bgtz, blez, bltz, bne, comparator_15_eq, comparator_16_eq,
       comparator_17_eq, comparator_18_eq, comparator_19_eq, comparator_20_eq, comparator_21_eq,
       comparator_22_eq, comparator_23_eq, comparator_24_eq, comparator_25_eq, comparator_26_eq,
       comparator_27_eq, comparator_29_eq, comparator_30_eq, comparator_31_eq, comparator_32_eq,
       comparator_33_eq, comparator_34_eq, comparator_35_eq, comparator_36_eq, comparator_37_eq, div, divu,
       mult, mulu, nop, \nor , \or , ori, pop, R_Basic, R_Special, R_Stack, rnd, slt, slti, sltiu, sltu, sub,
       \xor , xori;
  wire [8:1] or_7_out;

  Comparator #(.width(6)) comparator_1 (.a(in_1), .b(6'b001000), .eq(addi));  // open: gt, lt
  Comparator #(.width(6)) comparator_2 (.a(in_1), .b(6'b001010), .eq(slti));  // open: gt, lt
  Comparator #(.width(6)) comparator_3 (.a(in_1), .b(6'b001011), .eq(sltiu));  // open: gt, lt
  Comparator #(.width(6)) comparator_4 (.a(in_1), .b(6'b001100), .eq(andi));  // open: gt, lt
  Comparator #(.width(6)) comparator_5 (.a(in_1), .b(6'b001101), .eq(ori));  // open: gt, lt
  Comparator #(.width(6)) comparator_6 (.a(in_1), .b(6'b001110), .eq(xori));  // open: gt, lt
  Comparator #(.width(6)) comparator_7 (.a(in_1), .b(6'b100011), .eq(r_ram));  // open: gt, lt
  Comparator #(.width(6)) comparator_8 (.a(in_1), .b(6'b101011), .eq(w_ram));  // open: gt, lt
  Comparator #(.width(6)) comparator_9 (.a(in_1), .b(6'b000100), .eq(beq));  // open: gt, lt
  Comparator #(.width(6)) comparator_10 (.a(in_1), .b(6'b000101), .eq(bne));  // open: gt, lt
  Comparator #(.width(6)) comparator_11 (.a(in_1), .b(6'b000110), .eq(blez));  // open: gt, lt
  Comparator #(.width(6)) comparator_12 (.a(in_1), .b(6'b000111), .eq(bgtz));  // open: gt, lt
  Comparator #(.width(6)) comparator_13 (.a(in_1), .b(6'b000001), .eq(bltz));  // open: gt, lt
  Comparator #(.width(6)) comparator_14 (.a(in_1), .b({6{1'b0}}), .eq(R_Basic));  // open: gt, lt
  Comparator #(.width(6)) comparator_15 (.a(in_2), .b({6{1'b0}}), .eq(comparator_15_eq));  // open: gt, lt
  Comparator #(.width(6)) comparator_16 (.a(in_2), .b(6'b100000), .eq(comparator_16_eq));  // open: gt, lt
  Comparator #(.width(6)) comparator_17 (.a(in_2), .b(6'b100010), .eq(comparator_17_eq));  // open: gt, lt
  Comparator #(.width(6)) comparator_18 (.a(in_2), .b(6'b011000), .eq(comparator_18_eq));  // open: gt, lt
  Comparator #(.width(6)) comparator_19 (.a(in_2), .b(6'b011001), .eq(comparator_19_eq));  // open: gt, lt
  Comparator #(.width(6)) comparator_20 (.a(in_2), .b(6'b011010), .eq(comparator_20_eq));  // open: gt, lt
  Comparator #(.width(6)) comparator_21 (.a(in_2), .b(6'b011011), .eq(comparator_21_eq));  // open: gt, lt
  Comparator #(.width(6)) comparator_22 (.a(in_2), .b(6'b101010), .eq(comparator_22_eq));  // open: gt, lt
  Comparator #(.width(6)) comparator_23 (.a(in_2), .b(6'b101011), .eq(comparator_23_eq));  // open: gt, lt
  Comparator #(.width(6)) comparator_24 (.a(in_2), .b(6'b100100), .eq(comparator_24_eq));  // open: gt, lt
  Comparator #(.width(6)) comparator_25 (.a(in_2), .b(6'b100101), .eq(comparator_25_eq));  // open: gt, lt
  Comparator #(.width(6)) comparator_26 (.a(in_2), .b(6'b100111), .eq(comparator_26_eq));  // open: gt, lt
  Comparator #(.width(6)) comparator_27 (.a(in_2), .b(6'b101000), .eq(comparator_27_eq));  // open: gt, lt
  and and_1 (nop, R_Basic, comparator_15_eq);
  and and_2 (add, R_Basic, comparator_16_eq);
  and and_3 (sub, R_Basic, comparator_17_eq);
  and and_4 (mult, R_Basic, comparator_18_eq);
  and and_5 (mulu, R_Basic, comparator_19_eq);
  and and_6 (div, R_Basic, comparator_20_eq);
  and and_7 (divu, R_Basic, comparator_21_eq);
  and and_8 (slt, R_Basic, comparator_22_eq);
  and and_9 (sltu, R_Basic, comparator_23_eq);
  and and_10 (\and , R_Basic, comparator_24_eq);
  and and_11 (\or , R_Basic, comparator_25_eq);
  and and_12 (\nor , R_Basic, comparator_26_eq);
  and and_13 (\xor , R_Basic, comparator_27_eq);
  Comparator #(.width(6)) comparator_28 (.a(in_1), .b(6'b111000), .eq(R_Stack));  // open: gt, lt
  Comparator #(.width(6)) comparator_29 (.a(in_2), .b({6{1'b0}}), .eq(comparator_29_eq));  // open: gt, lt
  Comparator #(.width(6)) comparator_30 (.a(in_2), .b(6'b000001), .eq(comparator_30_eq));  // open: gt, lt
  Comparator #(.width(6)) comparator_31 (.a(in_2), .b(6'b001000), .eq(comparator_31_eq));  // open: gt, lt
  Comparator #(.width(6)) comparator_32 (.a(in_2), .b(6'b010000), .eq(comparator_32_eq));  // open: gt, lt
  Comparator #(.width(6)) comparator_33 (.a(in_2), .b(6'b010010), .eq(comparator_33_eq));  // open: gt, lt
  Comparator #(.width(6)) comparator_34 (.a(in_2), .b({6{1'b1}}), .eq(comparator_34_eq));  // open: gt, lt
  Comparator #(.width(6)) comparator_35 (.a(in_2), .b(6'b000001), .eq(comparator_35_eq));  // open: gt, lt
  Comparator #(.width(6)) comparator_36 (.a(in_2), .b(6'b000010), .eq(comparator_36_eq));  // open: gt, lt
  Comparator #(.width(6)) comparator_37 (.a(in_2), .b(6'b000100), .eq(comparator_37_eq));  // open: gt, lt
  nor nor_1 (Fill, andi, ori, xori);
  Comparator #(.width(6)) comparator_38 (.a(in_1), .b({6{1'b1}}), .eq(R_Special));  // open: gt, lt
  and and_14 (pop, R_Stack, comparator_29_eq);
  and and_15 (pop_push, R_Stack, comparator_30_eq);
  and and_16 (jr, R_Basic, comparator_31_eq);
  and and_17 (mfhi, R_Basic, comparator_32_eq);
  and and_18 (mflo, R_Basic, comparator_33_eq);
  and and_19 (halt, R_Special, comparator_34_eq);
  and and_20 (tty, R_Special, comparator_35_eq);
  and and_21 (rnd, R_Special, comparator_36_eq);
  and and_22 (kbd, R_Special, comparator_37_eq);
  or or_1 (or_7_out[3], slt, slti);
  or or_2 (or_7_out[4], sltu, sltiu);
  or or_3 (or_7_out[5], \and , andi);
  or or_4 (or_7_out[6], \or , ori);
  or or_5 (or_7_out[8], \xor , xori);
  or or_6 (stack, pop_push, pop);
  or or_7 (or_7_out[1], r_ram, w_ram, mfhi, kbd, mflo, add, addi);
  BitFinder #(.width(5)) bitfinder_1 (.in({bltz, bgtz, blez, bne, beq}), .index(Branch_OP), .found(Branch));
  BitFinder #(.width(4)) bitfinder_2 (.in({divu, div, mulu, mult}), .index(Hi_Lo_OP), .found(Hi_Lo_FLag));
  BitFinder #(.width(16)) bitfinder_3 (
    .in({{6{1'b0}}, rnd, or_7_out[8], \nor , or_7_out[6:3], sub, or_7_out[1], nop}), .index(ALU_OP));  // open: found

  // Other names for the same wires on the sheet: Func_Code[5:0] = in_2; lw = r_ram; OPCODE[5:0] = in_1;
  //   push = pop_push; sw = w_ram

  // Notes on the sheet:
  //   Inmediate Operations
  //   RAM Operations
  //   Inmediate Comparsions
  //   R-Basic Operations
  //   R-Stack Operations
  //   R-Other
  //   R-Specials
  //   Turn Constant into 32 bits
  //   Branch on Condition
  //   Flags
  //   Operations Mapper
endmodule

module Branch_Control (
  input  [31:0] Program_Counter,
  input  [25:0] J_Dest,
  input  J,
  input  jr,
  input  Branch,
  input  [2:0] Br_OP,
  input  [31:0] RS_V,
  input  [31:0] RT_V,
  input  Next,
  input  [15:0] Branch_Destiny,
  input  Ready,
  output [15:0] RAM_Addr,
  output [31:0] Next_Ptr
);

  wire beq, bgtz, blez, bltz, bne, comparator_2_eq, multiplexer_3_out;
  wire [31:0] adder_2_out, Br_Dest, Default, multiplexer_1_out, multiplexer_2_out, multiplexer_4_out;

  Adder #(.width(32)) adder_1 (.a(Program_Counter), .b({{29{1'b0}}, Next, 2'b00}), .out(Default));  // open: cin, cout
  Comparator #(.width(32)) comparator_1 (.a(RS_V), .b(RT_V), .eq(beq));  // open: gt, lt
  not not_1 (bne, beq);
  Comparator #(.width(32)) comparator_2 (.a(RS_V), .b({32{1'b0}}), .gt(bgtz), .eq(comparator_2_eq), .lt(bltz));
  Adder #(.width(32)) adder_2 (
    .a({{15{Branch_Destiny[15]}}, Branch_Destiny[14:0], 2'b00}), .b(32'h4), .out(adder_2_out));  // open: cin, cout
  or or_1 (blez, comparator_2_eq, bltz);
  Adder #(.width(32)) adder_3 (.a(Program_Counter), .b(adder_2_out), .out(Br_Dest));  // open: cin, cout
  Multiplexer #(.width(32), .enable("false")) multiplexer_1 (
    .in0(Default), .in1({Program_Counter[31:28], J_Dest, 2'b00}), .out(multiplexer_1_out), .sel(J));
  Multiplexer #(.width(32), .enable("false")) multiplexer_2 (
    .in0(multiplexer_1_out), .in1(RS_V), .out(multiplexer_2_out), .sel(jr));
  Multiplexer #(.select(3), .disabled(0)) multiplexer_3 (
    .in0(beq), .in1(bne), .in2(blez), .in3(bgtz), .in4(bltz), .out(multiplexer_3_out), .sel(Br_OP),
    .en(Branch));  // open: in5, in6, in7
  Multiplexer #(.width(32), .enable("false")) multiplexer_4 (
    .in0(multiplexer_2_out), .in1(Br_Dest), .out(multiplexer_4_out), .sel(multiplexer_3_out));
  Multiplexer #(.width(32), .enable("false")) multiplexer_5 (
    .in0(Program_Counter), .in1(multiplexer_4_out), .out(Next_Ptr), .sel(Ready));

  assign RAM_Addr = Program_Counter[19:4];

  // Other names for the same wires on the sheet: Jump[31:2] = {Program_Counter[31:28], J_Dest};
  //   PC[31:0] = Program_Counter
endmodule

module RAM_IO (
  input  in_1,
  input  in_2,
  input  [1:0] in_3,
  input  [31:0] RAM_Out_0,
  input  [31:0] RAM_Out_1,
  input  [31:0] RAM_Out_2,
  input  [31:0] RAM_Out_3,
  input  [31:0] Dir,
  input  [31:0] Value,
  input  in_10,
  input  in_11,
  input  [4:0] lw_reg,
  input  [4:0] Pop_Reg,
  input  [31:0] SP,
  output [3:0] Mask,
  output [15:0] RAM_Addr,
  output [31:0] RAM_In_0,
  output [31:0] RAM_Reading,
  output [31:0] RAM_In_1,
  output [31:0] RAM_In_2,
  output [31:0] RAM_In_3,
  output [4:0] Dest_Reg
);

  wire comparator_1_eq, comparator_2_eq, comparator_3_eq;
  wire [1:0] bank;
  wire [4:0] multiplexer_1_out;
  wire [31:0] Insert_2_q, Insert_q, multiplexer_2_out, SP_Acc, subtractor_1_out;

  Comparator #(.width(2)) comparator_1 (.a(in_3), .b(2'b00), .eq(comparator_1_eq));  // open: gt, lt
  Comparator #(.width(2)) comparator_2 (.a(in_3), .b(2'b00), .eq(comparator_2_eq));  // open: gt, lt
  Multiplexer #(.width(5), .enable("false")) multiplexer_1 (
    .in0(lw_reg), .in1(Pop_Reg), .out(multiplexer_1_out), .sel(in_2));
  Comparator #(.width(2)) comparator_3 (.a(in_3), .b(2'b00), .eq(comparator_3_eq));  // open: gt, lt
  // Probe on SP
  Multiplexer #(.width(32), .enable("false")) multiplexer_2 (
    .in0(Dir), .in1(SP_Acc), .out(multiplexer_2_out), .sel(in_2));
  Register #(.width(32)) Insert (
    .D(multiplexer_2_out), .en(comparator_1_eq), .Q({Insert_q[31:20], RAM_Addr, bank, Insert_q[1:0]}),
    .clk(in_10), .clr(in_11));
  Register #(.width(32)) Insert_2 (.D(Value), .en(comparator_2_eq), .Q(Insert_2_q), .clk(in_10), .clr(in_11));
  Register #(.width(5)) u_Dest_Reg (
    .D(multiplexer_1_out), .en(comparator_3_eq), .Q(Dest_Reg), .clk(in_10), .clr(in_11));
  Subtractor #(.width(32)) subtractor_1 (.a(SP), .b(32'h4), .out(subtractor_1_out));  // open: bin, bout
  // Probe on {Insert_q[31:20], RAM_Addr, bank, Insert_q[1:0]}
  // Probe on Insert_2_q
  Multiplexer #(.width(32), .enable("false")) multiplexer_3 (
    .in0(SP), .in1(subtractor_1_out), .out(SP_Acc), .sel(in_1));
  Decoder #(.select(2), .enable("false")) decoder_1 (
    .out0(Mask[0]), .out1(Mask[1]), .out2(Mask[2]), .out3(Mask[3]), .sel(bank));
  Demultiplexer #(.select(2), .width(32), .enable("false")) demultiplexer_1 (
    .out0(RAM_In_0), .out1(RAM_In_1), .out2(RAM_In_2), .out3(RAM_In_3), .in(Insert_2_q), .sel(bank));
  Multiplexer #(.select(2), .width(32), .enable("false")) multiplexer_4 (
    .in0(RAM_Out_0), .in1(RAM_Out_1), .in2(RAM_Out_2), .in3(RAM_Out_3), .out(RAM_Reading), .sel(bank));

  // Other names for the same wires on the sheet: CLK = in_10; pop_push = in_1; RST = in_11; stack = in_2;
  //   State[1:0] = in_3
endmodule

module State_Machine (
  input  in_1,
  input  in_2,
  input  in_3,
  input  in_4,
  input  in_5,
  input  in_6,
  input  [3:0] in_7,
  input  [3:0] in_8,
  input  in_9,
  input  [15:0] in_10,
  output [1:0] State,
  output RW,
  output Ready,
  output Stop
);

  wire and_1_out, and_2_out, comparator_1_eq, d_ff_2_q, not_1_out, or_1_out, or_2_out, or_3_out, or_4_out,
       or_5_out, Prev_Op;
  wire [1:0] multiplexer_2_out, multiplexer_3_out;
  wire [3:0] Countr_q, Time;
  wire [15:0] register_1_q;

  Multiplexer #(.width(4), .enable("false")) multiplexer_1 (.in0(in_7), .in1(in_8), .out(Time), .sel(Prev_Op));
  Multiplexer #(.width(2), .enable("false")) multiplexer_2 (
    .in0(2'b00), .in1(2'b01), .out(multiplexer_2_out), .sel(or_1_out));
  or or_1 (or_1_out, in_4, and_1_out);
  and and_1 (and_1_out, in_5, in_6);
  Register #(.width(16)) register_1 (.D(in_10), .Q(register_1_q), .clk(in_1), .clr(in_2));  // open: en
  D_Flip_Flop d_ff_1 (.clk(in_1), .D(or_2_out), .Q(Prev_Op), .en(Ready), .reset(in_2));  // open: Qn, preset
  or or_2 (or_2_out, in_4, in_5);
  Multiplexer #(.width(2), .enable("false")) multiplexer_3 (
    .in0(multiplexer_2_out), .in1(2'b10), .out(multiplexer_3_out), .sel(or_3_out));
  or or_3 (or_3_out, and_2_out, in_3);
  and and_2 (and_2_out, in_6, ~in_5);  // AND_Gate
  Comparator #(.width(16)) comparator_1 (.a(register_1_q), .b(in_10), .eq(comparator_1_eq));  // open: gt, lt
  Counter #(.width(4), .max('hf)) Countr (.Q(Countr_q), .clk(in_1), .clr(or_4_out));  // open: load, D, count, carry
  or or_4 (or_4_out, d_ff_2_q, not_1_out, in_2);
  D_Flip_Flop d_ff_2 (.clk(in_1), .D(Ready), .Q(d_ff_2_q), .reset(in_2));  // open: Qn, preset, en
  not not_1 (not_1_out, comparator_1_eq);
  Register #(.width(2)) u_State (.D(multiplexer_3_out), .en(Ready), .Q(State), .clk(in_1), .clr(in_2));
  // Probe on Countr_q
  Comparator #(.width(4)) comparator_2 (.a(Countr_q), .b(Time), .eq(Ready));  // open: gt, lt
  or or_5 (or_5_out, in_9, Stop);
  D_Flip_Flop Halted (.clk(in_1), .D(or_5_out), .Q(Stop), .reset(in_2));  // open: Qn, preset, en
  Comparator #(.width(2)) comparator_3 (.a(State), .b(2'b01), .eq(RW));  // open: gt, lt

  // Other names for the same wires on the sheet: Addr[15:0] = in_10; CLK = in_1; CLR = in_2; Halt = in_9;
  //   pop_push = in_5; r_ram = in_3; Read_Time[3:0] = in_7; stack = in_6; w_ram = in_4; Write_Time[3:0] = in_8
endmodule

module Signed_Mult (
  input  [31:0] in_1,
  input  [31:0] in_2,
  output [31:0] Lo,
  output [31:0] Hi
);

  wire A_Sign, adder_1_cout, B_Sign, P_Sign;
  wire [31:0] abs_1_absolute_val, abs_2_absolute_val, HiS, HiU, LoS, LoU, not_1_out, not_2_out;

  // Probe on in_1
  Sign sign_1 (.Input(in_1), .Sign(A_Sign));
  // Probe on in_2
  Sign sign_2 (.Input(in_2), .Sign(B_Sign));
  xor xor_1 (P_Sign, A_Sign, B_Sign);
  Abs abs_1 (.Input(in_1), .Absolute_Val(abs_1_absolute_val));
  Abs abs_2 (.Input(in_2), .Absolute_Val(abs_2_absolute_val));
  assign not_1_out = ~LoU;  // NOT_Gate not_1, 32 bits wide
  assign not_2_out = ~HiU;  // NOT_Gate not_2, 32 bits wide
  Multiplier #(.width(32)) multiplier_1 (
    .a(abs_1_absolute_val), .b(abs_2_absolute_val), .out(LoU), .cout(HiU));  // open: cin
  Adder #(.width(32)) adder_1 (.a(not_1_out), .b(32'h1), .out(LoS), .cout(adder_1_cout));  // open: cin
  Adder #(.width(32)) adder_2 (.a({32{1'b0}}), .b(not_2_out), .out(HiS), .cin(adder_1_cout));  // open: cout
  Multiplexer #(.width(32), .enable("false")) multiplexer_1 (.in0(LoU), .in1(LoS), .out(Lo), .sel(P_Sign));
  Multiplexer #(.width(32), .enable("false")) multiplexer_2 (.in0(HiU), .in1(HiS), .out(Hi), .sel(P_Sign));
  // Probe on Lo
  // Probe on Hi
endmodule

module Signed_Div (
  input  [31:0] in_1,
  input  [31:0] in_2,
  output [31:0] Quotient,
  output [31:0] Remainder
);

  wire A_Sign, B_Sign, xor_1_out;
  wire [31:0] abs_1_absolute_val, abs_2_absolute_val, divider_1_out, neg_1_negative;

  // Probe on in_1
  Sign sign_1 (.Input(in_1), .Sign(A_Sign));
  // Probe on in_2
  Sign sign_2 (.Input(in_2), .Sign(B_Sign));
  Abs abs_1 (.Input(in_1), .Absolute_Val(abs_1_absolute_val));
  Abs abs_2 (.Input(in_2), .Absolute_Val(abs_2_absolute_val));
  Divider #(.width(32)) divider_1 (
    .a(abs_1_absolute_val), .b(abs_2_absolute_val), .out(divider_1_out), .rem(Remainder));  // open: upper
  Neg neg_1 (.Input(divider_1_out), .Negative(neg_1_negative));
  xor xor_1 (xor_1_out, A_Sign, B_Sign);
  Multiplexer #(.width(32), .enable("false")) multiplexer_1 (
    .in0(divider_1_out), .in1(neg_1_negative), .out(Quotient), .sel(xor_1_out));
  // Probe on Quotient
  // Probe on Remainder

  // Other names for the same wires on the sheet: A[31:0] = in_1
endmodule

module Abs (
  input  [31:0] Input,
  output [31:0] Absolute_Val
);

  wire sign_1_sign;
  wire [31:0] not_1_out, subtractor_1_out;

  // Probe on Input
  assign not_1_out = ~Input;  // NOT_Gate not_1, 32 bits wide
  Subtractor #(.width(32)) subtractor_1 (.a(not_1_out), .b({32{1'b1}}), .out(subtractor_1_out));  // open: bin, bout
  Sign sign_1 (.Input(Input), .Sign(sign_1_sign));
  // Probe on Absolute_Val
  Multiplexer #(.width(32), .enable("false")) multiplexer_1 (
    .in0(Input), .in1(subtractor_1_out), .out(Absolute_Val), .sel(sign_1_sign));

  // Other names for the same wires on the sheet: In[31:0] = Input
endmodule

module Sign (
  input  [31:0] Input,
  output Sign
);


  assign Sign = Input[31];
endmodule

module Neg (
  input  [31:0] Input,
  output [31:0] Negative
);

  wire [31:0] not_1_out;

  // Probe on Input
  assign not_1_out = ~Input;  // NOT_Gate not_1, 32 bits wide
  Adder #(.width(32)) adder_1 (.a(not_1_out), .b(32'h1), .out(Negative));  // open: cin, cout
  // Probe on Negative
endmodule

module Delayer (
  input  [3:0] Time,
  input  Clock,
  input  Start,
  output Output
);

  wire not_1_out, or_1_out, subtractor_1_bout;
  wire [3:0] multiplexer_1_out, Next, register_1_q;

  Multiplexer #(.width(4), .enable("false")) multiplexer_1 (
    .in0(Next), .in1(Time), .out(multiplexer_1_out), .sel(Start));
  or or_1 (or_1_out, Start, not_1_out);
  not not_1 (not_1_out, subtractor_1_bout);
  Register #(.width(4)) register_1 (.D(multiplexer_1_out), .en(or_1_out), .Q(register_1_q), .clk(Clock));  // open: clr
  Comparator #(.width(4)) comparator_1 (.a(register_1_q), .b(4'b0000), .gt(Output));  // open: eq, lt
  Subtractor #(.width(4)) subtractor_1 (
    .a(register_1_q), .b(4'b0001), .out(Next), .bout(subtractor_1_bout));  // open: bin
endmodule
